# Fritzing sketch CircuitoDuckHunt (saved by Fritzing 0.8.7b)
circuit board: 8.46667cm x 5.64444cm
breadboards: 1

parts:
  Parte1 = Arduino Nano (Rev3.0)
  R1 = Resistor [tolerance=±5% resistance=10k package=THT]
  R2 = Photocell (LDR) [package=THT]
  S1 = Momentary Switch [package=ksa_sealed_tac_switch]
  VCC1 = Battery block 9V
  R3 = Resistor [tolerance=±5% resistance=10k package=THT]

nets:
  N1: Parte1.GND, R1.Pin_0, VCC1.-, R3.Pin_1
  N2: Parte1.D12/MISO, S1.4, R3.Pin_0
  N3: Parte1.VIN, VCC1.+
  N4: Parte1.5V, R2.pin_0, S1.2
  N5: Parte1.A0, R1.Pin_1, R2.pin_1
